# Fritzing sketch Deepakfinalpcb (saved by Fritzing 0.9.3b)
circuit board: 6.74955cm x 5.69576cm

parts:
  Raspberry_Pi_1 = Raspberry Pi 3 [part_number=RPI-3-V1.2]
  IC1 = L293D [package=THT]
  M1 = DC Motor
  VCC1 = 4 x AAA Battery Mount
  M2 = DC Motor

nets:
  N1: Raspberry_Pi_1.GIPO10, IC1.In_4
  N2: Raspberry_Pi_1.GIPO9, IC1.In_3
  N3: Raspberry_Pi_1.GIPO11, IC1.Enable_2
  N4: Raspberry_Pi_1.GND, IC1.0V, VCC1.-
  N5: Raspberry_Pi_1.GIPO25, IC1.Enable_1
  N6: Raspberry_Pi_1.GIPO24, IC1.In_1
  N7: Raspberry_Pi_1.GIPO23, IC1.In_2
  N8: Raspberry_Pi_1.5V, IC1.+V
  N9: IC1.Out_1_(_Controlled_by_Enable_1_), M1.pin_2
  N10: IC1.Out_2_(_Controlled_by_Enable_1_), M1.pin_1
  N11: IC1.+Vmotor, VCC1.+
  N12: IC1.Out_3_(_Controlled_by_Enable_2_), M2.pin_2
  N13: IC1.Out_4_(_Controlled_by_Enable_2_), M2.pin_1
