# Fritzing sketch MergedPCBbyTRIPLED'S (saved by Fritzing 0.9.3b)
circuit board: 8.75222cm x 6.54701cm
breadboards: 1

parts:
  IC2 = L293D [package=THT]
  M2 = DC Motor
  M1 = DC Motor
  J1 = Infrared Proximity Sensor
  HC-SR04_Sensor_1 = HC-SR04 Ultrasonic Distance Sensor
  Raspberry_Pi_1 = Raspberry Pi 3 [part_number=RPI-3-V1.2]
  JP4 = Header 6 [package=molex-1x6-ra]
  R1 = Resistor [tolerance=±5% resistance=1k package=THT]
  R2 = Resistor [tolerance=±5% resistance=220 package=THT]

nets:
  N1: IC2.Enable_1, Raspberry_Pi_1.GPIO22
  N2: IC2.In_1, Raspberry_Pi_1.GPIO27
  N3: IC2.Out_1_(_Controlled_by_Enable_1_), M2.pin_1
  GND: IC2.0V, J1.GND, HC-SR04_Sensor_1.GND, Raspberry_Pi_1.GND, JP4.5, JP4.6, R2.Pin_1
  N4: IC2.Out_2_(_Controlled_by_Enable_1_), M2.pin_2
  N5: IC2.In_2, Raspberry_Pi_1.GPIO17
  N6: IC2.+Vmotor, JP4.1
  N7: IC2.Enable_2, Raspberry_Pi_1.GPIO26
  N8: IC2.In_3, Raspberry_Pi_1.GPIO19
  N9: IC2.Out_3_(_Controlled_by_Enable_2_), M1.pin_2
  N10: IC2.Out_4_(_Controlled_by_Enable_2_), M1.pin_1
  N11: IC2.In_4, Raspberry_Pi_1.GPIO13
  VCC: IC2.+V, J1.Vcc, HC-SR04_Sensor_1.VCC, Raspberry_Pi_1.5V
  N12: J1.Vout, Raspberry_Pi_1.GPIO14
  N13: HC-SR04_Sensor_1.TRIG, Raspberry_Pi_1.GPIO4
  N14: HC-SR04_Sensor_1.ECHO, R1.Pin_0
  N15: Raspberry_Pi_1.GPIO10, R1.Pin_1, R2.Pin_0

notes:
  David Asare
  Rover PCB
  Deepak Singh
  Darrel Asare
  VCC
  GND
  VOUT
  3V
  USB PWR
  2K
  1K
