# Fritzing sketch RPI Speed Sensor2 (saved by Fritzing 0.9.3b)
circuit board: 6.91389cm x 2.84694cm
breadboards: 1

parts:
  Raspberry_Pi_1 = Raspberry Pi 3 [part_number=RPI-3-V1.2]
  J1 = Infrared Proximity Sensor

nets:
  GND: Raspberry_Pi_1.GND, J1.GND
  N1: Raspberry_Pi_1.GIPO21, J1.Vout
  5V: Raspberry_Pi_1.5V, J1.Vcc

notes:
  Darrel Asare
  LM393 Speed Sensor
