# Fritzing sketch Ultrasonic Sensor-DavidAsare (saved by Fritzing 0.9.3b)
circuit board: 6.48566cm x 4.65851cm
breadboards: 1

parts:
  Raspberry_Pi_1 = Raspberry Pi 3 [part_number=RPI-3-V1.2]
  HC-SR04_Sensor_1 = HC-SR04 Ultrasonic Distance Sensor
  R1 = Resistor [tolerance=±20% resistance=1k package=THT]
  R2 = Resistor [tolerance=±5% resistance=2k package=THT]

nets:
  N1: Raspberry_Pi_1.GPIO4, HC-SR04_Sensor_1.TRIG
  N2: Raspberry_Pi_1.GPIO17, R1.Pin_1, R2.Pin_1
  GND: Raspberry_Pi_1.GND, HC-SR04_Sensor_1.GND, R2.Pin_0
  5V: Raspberry_Pi_1.5V, HC-SR04_Sensor_1.VCC
  N3: HC-SR04_Sensor_1.ECHO, R1.Pin_0

notes:
  David Asare
  Distance Sensor
  R1
  R2
